# Fritzing sketch submorse_controller (saved by Fritzing 0.9.9b)

parts:
  Part1 = Adafruit Trinket M0 [part_number="Adafruit #3500"]
  D1_1N4148 = Diode [package=diode-1n4148]
  R1 = Resistor [tolerance=±5% resistance=100k package="0402 [SMD]"]
  R2 = Resistor [tolerance=±5% resistance=1k package="0402 [SMD]"]
  C1_0_1uF = Capacitor [package=cap-pth-large]
  S1 = Momentary Switch [package=ksa_sealed_tac_switch]

nets:
  N1: Part1.GND, C1_0_1uF.1, S1.3
  N2: Part1.3.3V, R1.Pin_0
  N3: Part1.D0_A4_PA08_SDA, D1_1N4148.C, R2.Pin_0, C1_0_1uF.2
  N4: D1_1N4148.A, R1.Pin_1, R2.Pin_1, S1.1
